// Logisim project Live Circuit.circ as structural Verilog: 1 circuit, main circuit main
module main (
  output [3:0] out_1
);

  wire and_1_out, and_2_out, and_3_out, and_4_out, and_5_out, and_6_out, and_7_out, and_8_out, and_9_out,
       and_10_out, and_11_out, and_12_out, and_13_out, clock_1_out, j_k_ff_1_qn, j_k_ff_2_qn, j_k_ff_3_qn,
       j_k_ff_4_qn, or_1_out, or_2_out, or_3_out, or_4_out, or_5_out, or_6_out, or_7_out, or_8_out;

  Clock clock_1 (.out(clock_1_out));
  J_K_Flip_Flop j_k_ff_1 (
    .J(or_1_out), .clk(clock_1_out), .K(or_8_out), .Q(out_1[0]), .Qn(j_k_ff_1_qn));  // open: preset, en, reset
  J_K_Flip_Flop j_k_ff_2 (
    .J(or_2_out), .clk(clock_1_out), .K(or_3_out), .Q(out_1[1]), .Qn(j_k_ff_2_qn));  // open: preset, en, reset
  J_K_Flip_Flop j_k_ff_3 (
    .J(or_4_out), .clk(clock_1_out), .K(or_5_out), .Q(out_1[2]), .Qn(j_k_ff_3_qn));  // open: preset, en, reset
  J_K_Flip_Flop j_k_ff_4 (
    .J(or_6_out), .clk(clock_1_out), .K(or_7_out), .Q(out_1[3]), .Qn(j_k_ff_4_qn));  // open: preset, en, reset
  and and_1 (and_1_out, j_k_ff_1_qn, j_k_ff_2_qn);
  or or_1 (or_1_out, and_1_out, and_2_out);
  and and_2 (and_2_out, out_1[2], j_k_ff_4_qn);
  and and_3 (and_3_out, out_1[0], out_1[1]);
  and and_4 (and_4_out, and_3_out, j_k_ff_3_qn);
  and and_5 (and_5_out, out_1[0], j_k_ff_3_qn, out_1[3]);
  and and_6 (and_6_out, and_3_out, out_1[3]);
  and and_7 (and_7_out, j_k_ff_2_qn, and_8_out);
  and and_8 (and_8_out, out_1[2], j_k_ff_4_qn);
  or or_2 (or_2_out, and_8_out, and_9_out);
  and and_9 (and_9_out, j_k_ff_1_qn, j_k_ff_2_qn, out_1[2]);
  and and_10 (and_10_out, out_1[1], j_k_ff_3_qn, j_k_ff_4_qn);
  or or_3 (or_3_out, and_10_out, and_11_out);
  and and_11 (and_11_out, and_6_out, out_1[2]);
  and and_12 (and_12_out, j_k_ff_1_qn, j_k_ff_4_qn);
  or or_4 (or_4_out, and_12_out, and_13_out);
  and and_13 (and_13_out, and_5_out, j_k_ff_2_qn);
  or or_5 (or_5_out, and_12_out, and_6_out);
  or or_6 (or_6_out, and_3_out, and_10_out, and_9_out);
  or or_7 (or_7_out, and_3_out, and_5_out, and_9_out);
  or or_8 (or_8_out, and_4_out, and_5_out, and_6_out, and_7_out);
endmodule
