// Logisim project L1-E2.circ as structural Verilog: 1 circuit, main circuit main
module main (
  input  in_1,
  input  in_2,
  input  in_3,
  input  in_4,
  input  in_5,
  input  in_6,
  output out_7
);

  wire and_1_out, and_2_out, and_3_out, and_4_out;

  and and_1 (and_1_out, in_1, in_2);
  and and_2 (and_2_out, and_1_out, in_3);
  and and_3 (and_3_out, and_2_out, in_4);
  and and_4 (and_4_out, and_3_out, in_5);
  and and_5 (out_7, and_4_out, in_6);

  // Notes on the sheet:
  //   Name: Joy Kumar Ghosh
  //   ID: 2211424642
  //   Experiment - 2
endmodule
