// Logisim project L2-E1.circ as structural Verilog: 1 circuit, main circuit main
module main (
  input  A,
  input  B,
  input  C,
  output out_4
);

  wire nand_1_out, nand_2_out, nand_3_out;

  nand nand_1 (nand_1_out, C, C);
  nand nand_2 (nand_2_out, A, C);
  nand nand_3 (nand_3_out, B, nand_1_out);
  nand nand_4 (out_4, nand_2_out, nand_3_out);

  // Notes on the sheet:
  //   ID: 2211424 6 42
  //   Lab - 02
  //   Name: Joy Kumar Ghosh
endmodule
