// Logisim project L5-E1.circ as structural Verilog: 1 circuit, main circuit main
module main (
  input  A0,
  input  B0,
  input  Cin,
  input  A1,
  input  B1,
  input  A2,
  input  B2,
  input  A3,
  input  B3,
  output Cout
);

  wire and_1_out, and_2_out, and_3_out, and_4_out, and_5_out, and_6_out, and_7_out, and_8_out, or_1_out,
       or_2_out, or_3_out, xor_1_out, xor_2_out, xor_3_out, xor_4_out;
  wire [3:0] xor_5_out;

  xor xor_1 (xor_1_out, A0, B0);
  xor xor_2 (xor_2_out, A1, B1);
  xor xor_3 (xor_3_out, A2, B2);
  xor xor_4 (xor_4_out, A3, B3);
  xor xor_5 (xor_5_out[0], xor_1_out, Cin);
  and and_1 (and_1_out, Cin, xor_1_out);
  and and_2 (and_2_out, A0, B0);
  xor xor_6 (xor_5_out[1], xor_2_out, or_1_out);
  and and_3 (and_3_out, or_1_out, xor_2_out);
  and and_4 (and_4_out, A1, B1);
  xor xor_7 (xor_5_out[2], xor_3_out, or_2_out);
  and and_5 (and_5_out, or_2_out, xor_3_out);
  and and_6 (and_6_out, A2, B2);
  xor xor_8 (xor_5_out[3], xor_4_out, or_3_out);
  and and_7 (and_7_out, or_3_out, xor_4_out);
  and and_8 (and_8_out, A3, B3);
  or or_1 (or_1_out, and_1_out, and_2_out);
  or or_2 (or_2_out, and_3_out, and_4_out);
  or or_3 (or_3_out, and_5_out, and_6_out);
  or or_4 (Cout, and_7_out, and_8_out);
  // Probe on xor_5_out

  // Notes on the sheet:
  //   Cin
  //   Cin
  //   Cin
  //   Cout
  //   Cout
  //   Cout
  //   Cout
  //   Carry = 0
  //   Sum
  //   ID: 2211424642
  //   Lab: 05
  //   Group: 05
  //   A = 4 = 0100 = A3 A2 A1 A0
  //   B = 7 = 0111 = B3 B2 B1 B0
  //   Sum = 4 + 7 = 11 = 1011
  //   Name: Joy Kumar Ghosh
endmodule
