// Logisim project L6-E1.circ as structural Verilog: 1 circuit, main circuit main
module main (
  input  in_1,
  input  A,
  input  B,
  input  C,
  output out_5
);

  wire and_1_out, and_2_out, and_3_out, and_4_out, not_1_out, not_2_out, not_3_out, or_1_out, or_2_out;

  not not_1 (not_1_out, A);
  not not_2 (not_2_out, B);
  not not_3 (not_3_out, C);
  and and_1 (and_1_out, not_3_out, not_1_out, not_2_out);
  and and_2 (and_2_out, 1'b1, not_1_out, B);
  and and_3 (and_3_out, in_1, A, not_2_out);
  and and_4 (and_4_out, not_3_out, A, B);
  or or_1 (or_1_out, and_1_out, and_2_out);
  or or_2 (or_2_out, and_3_out, and_4_out);
  or or_3 (out_5, or_1_out, or_2_out);

  // Notes on the sheet:
  //   l0
  //   l1
  //   l2
  //   l3
  //   Group: 05
  //   Name: Joy Kumar Ghosh
  //   ID: 2211424642
endmodule
