// Logisim project L7-E1.circ as structural Verilog: 1 circuit, main circuit main
module main (
  input  K,
  input  J,
  input  K_2,
  input  J_2,
  output Q,
  output Q_prime,
  output Q_2,
  output Q_prime_2
);

  wire and_1_out, and_2_out, and_3_out, and_4_out, clock_1_out, clock_2_out;

  Clock clock_1 (.out(clock_1_out));
  Clock clock_2 (.out(clock_2_out));
  and and_1 (and_1_out, Q, K, clock_1_out);
  and and_2 (and_2_out, clock_1_out, J, Q_prime);
  and and_3 (and_3_out, Q_2, K_2, clock_2_out);
  and and_4 (and_4_out, clock_2_out, J_2, Q_prime_2);
  nor nor_1 (Q, and_1_out, Q_prime);
  nor nor_2 (Q_prime, Q, and_2_out);
  nor nor_3 (Q_2, and_3_out, Q_prime_2);
  nor nor_4 (Q_prime_2, Q_2, and_4_out);

  // Notes on the sheet:
  //   CLK
  //   CLK
  //   Group: 05
  //   Joy Kumar Ghosh
  //   ID: 2211424642
endmodule
