// Logisim project L8-E1.circ as structural Verilog: 1 circuit, main circuit main
module main (
  input  X
);

  wire and_1_out, and_2_out, clock_1_out, j_k_ff_1_q, j_k_ff_1_qn, j_k_ff_2_q, not_1_out;

  not not_1 (not_1_out, X);
  Clock clock_1 (.out(clock_1_out));
  and and_1 (and_1_out, j_k_ff_1_qn, not_1_out);
  J_K_Flip_Flop j_k_ff_1 (
    .J(X), .clk(clock_1_out), .K(X), .Q(j_k_ff_1_q), .Qn(j_k_ff_1_qn));  // open: preset, en, reset
  J_K_Flip_Flop j_k_ff_2 (.J(and_1_out), .clk(clock_1_out), .K(X), .Q(j_k_ff_2_q));  // open: Qn, preset, en, reset
  LED led_1 (.in(j_k_ff_1_q));
  and and_2 (and_2_out, j_k_ff_1_qn, X);
  LED led_2 (.in(j_k_ff_2_q));
  LED led_3 (.in(and_2_out));

  // Notes on the sheet:
  //   CLK
  //   A
  //   B
  //   Y
  //   Joy Kumar Ghosh
  //   ID: 2211424642
  //   Group: 05
endmodule
