// Logisim project Minimal 1st canonical circuit of BCD to Excess-3 converter.circ as structural Verilog: 1 circuit, main circuit main
// Output
module main (
  input  W,
  input  X,
  input  Y,
  input  Z,
  output [3:0] Output__Excess_3
);

  wire _4073_out, _7404_2_out, _7404_out, _7408_2_out, _7408_3_out, _7408_4_out, _7408_5_out, _7408_6_out,
       _7408_out;

  not _7404 (_7404_out, X);
  not _7404_2 (_7404_2_out, Y);
  not _7404_3 (Output__Excess_3[0], Z);
  and _7408 (_7408_out, X, Y);
  and _7408_2 (_7408_2_out, X, Z);
  and _7408_3 (_7408_3_out, _7404_out, Z);
  and _7408_4 (_7408_4_out, _7404_out, Y);
  and _4073 (_4073_out, X, _7404_2_out, Output__Excess_3[0]);
  and _7408_5 (_7408_5_out, _7404_2_out, Output__Excess_3[0]);
  and _7408_6 (_7408_6_out, Y, Z);
  or _4075 (Output__Excess_3[3], W, _7408_out, _7408_2_out);
  or _4075_2 (Output__Excess_3[2], _7408_3_out, _7408_4_out, _4073_out);
  or _7432 (Output__Excess_3[1], _7408_5_out, _7408_6_out);

  // Notes on the sheet:
  //   1
  //   2
  //   3
  //   4
  //   5
  //   6
  //   1
  //   2
  //   4
  //   5
  //   9
  //   10
  //   12
  //   13
  //   1
  //   2
  //   8
  //   1
  //   2
  //   4
  //   5
  //   3
  //   1
  //   2
  //   8
  //   6
  //   8
  //   11
  //   9
  //   3
  //   6
  //   9
  //   3
  //   6
  //   4
  //   5
  //   1
  //   3
  //   2
  //   A
  //   B
  //   C
  //   D
  //   Apparatus:
  //   1 x IC 7404
  //   2 x IC 7408
  //   1 x IC 7432
  //   1 x IC 4073
  //   1 x IC 4075
endmodule
