// Logisim project Boolean Algebra - Copy.circ as structural Verilog: 1 circuit, main circuit main
module main (
  input  A,
  input  B,
  input  C,
  input  D
);

  wire and_1_out, and_2_out, and_3_out, and_4_out, and_5_out, and_6_out, and_7_out, and_8_out, and_9_out,
       and_10_out, and_11_out, and_12_out, and_13_out, and_14_out, and_15_out, and_16_out, and_17_out,
       and_18_out, and_19_out, and_20_out, not_1_out, not_2_out, not_3_out, not_4_out, not_5_out, not_6_out,
       not_7_out, not_8_out, not_9_out, not_10_out, or_1_out, or_2_out, or_3_out, or_4_out, or_5_out,
       or_6_out, or_7_out, or_8_out, or_9_out, or_10_out, or_11_out, or_12_out, or_13_out, or_14_out,
       or_15_out, xnor_1_out, xnor_2_out, xnor_3_out;

  not not_1 (not_1_out, A);
  not not_2 (not_2_out, B);
  not not_3 (not_3_out, C);
  not not_4 (not_4_out, D);
  and and_1 (and_1_out, C, D);
  or or_1 (or_1_out, B, D);
  and and_2 (and_2_out, not_1_out, not_2_out);
  or or_2 (or_2_out, A, C);
  and and_3 (and_3_out, not_2_out, C);
  and and_4 (and_4_out, B, not_3_out);
  and and_5 (and_5_out, not_1_out, D);
  and and_6 (and_6_out, not_1_out, B);
  and and_7 (and_7_out, A, C);
  or or_3 (or_3_out, not_1_out, B);
  xnor xnor_1 (xnor_1_out, B, D);
  not not_5 (not_5_out, or_1_out);
  xnor xnor_2 (xnor_2_out, A, C);
  and and_8 (and_8_out, and_2_out, xnor_3_out);
  xnor xnor_3 (xnor_3_out, C, D);
  not not_6 (not_6_out, or_2_out);
  or or_4 (or_4_out, and_3_out, and_4_out);
  and and_9 (and_9_out, not_5_out, C);
  and and_10 (and_10_out, and_6_out, D);
  and and_11 (and_11_out, and_1_out, and_2_out);
  and and_12 (and_12_out, and_4_out, not_4_out);
  or or_5 (or_5_out, and_7_out, D);
  not not_7 (not_7_out, and_1_out);
  or or_6 (or_6_out, not_10_out, not_1_out);
  and and_13 (and_13_out, and_12_out, A);
  and and_14 (and_14_out, xnor_1_out, not_3_out);
  or or_7 (or_7_out, and_14_out, and_1_out);
  and and_15 (and_15_out, not_5_out, xnor_2_out);
  or or_8 (or_8_out, B, C);
  not not_8 (not_8_out, or_8_out);
  and and_16 (and_16_out, or_4_out, and_5_out);
  or or_9 (or_9_out, and_9_out, and_10_out);
  not not_9 (not_9_out, and_11_out);
  not not_10 (not_10_out, and_12_out);
  or or_10 (or_10_out, or_5_out, not_2_out);
  or or_11 (or_11_out, or_3_out, not_7_out);
  and and_17 (and_17_out, or_7_out, not_1_out);
  or or_12 (or_12_out, and_15_out, and_8_out);
  and and_18 (and_18_out, xnor_1_out, not_6_out);
  or or_13 (or_13_out, not_8_out, and_16_out);
  and and_19 (and_19_out, not_9_out, not_10_out);
  and and_20 (and_20_out, or_10_out, or_11_out);
  or or_14 (or_14_out, and_17_out, and_15_out);
  or or_15 (or_15_out, or_12_out, and_18_out);
  _7_Segment_Display u_7_segment_display_1 (
    .g(or_6_out), .f(and_20_out), .a(or_14_out), .b(or_15_out), .e(and_19_out), .d(or_9_out), .c(or_13_out),
    .dp(and_13_out));

  // Notes on the sheet:
  //   3x X-NOR GATE: 1x4077-2 Input X-NOR IC
  //   20x AND GATE: 5X 7408-2 Input AND IC
  //   15x OR GATE: 4x 7432 2-Input OR IC
  //   10x NOT GATE: 2X 7404 NOT IC
  //   g f a b
  //   e d c h
  //   Bolean Algebra
  //   Group: 05
endmodule
