// Logisim project Decoder - Most Efficient with pin.circ as structural Verilog: 1 circuit, main circuit main
module main (
  input  [3:0] in_1
);

  wire a_out, b_out, c_out, d_out, decoder_1_out0, decoder_1_out1, decoder_1_out2, decoder_1_out3,
       decoder_1_out4, decoder_1_out5, decoder_1_out6, decoder_1_out7, decoder_1_out8, decoder_1_out9,
       decoder_1_out10, decoder_1_out11, decoder_1_out12, e_out, f_out, g_out, or_1_out, u_out, v_out, x_out,
       y_out, z_out;

  Decoder #(.select(4)) decoder_1 (
    .out0(decoder_1_out0), .out1(decoder_1_out1), .out2(decoder_1_out2), .out3(decoder_1_out3),
    .out4(decoder_1_out4), .out5(decoder_1_out5), .out6(decoder_1_out6), .out7(decoder_1_out7),
    .out8(decoder_1_out8), .out9(decoder_1_out9), .out10(decoder_1_out10), .out11(decoder_1_out11),
    .out12(decoder_1_out12), .sel(in_1), .en(1'b1));  // open: out13, out14, out15
  or x (x_out, decoder_1_out0, decoder_1_out3, decoder_1_out5);
  or y (y_out, decoder_1_out1, decoder_1_out8, decoder_1_out9);
  or z (z_out, decoder_1_out7, decoder_1_out10);
  or u (u_out, decoder_1_out2, decoder_1_out5);
  or v (v_out, decoder_1_out6, decoder_1_out11);
  or a (a_out, x_out, z_out);
  or b (b_out, x_out, decoder_1_out10);
  or c (c_out, x_out, y_out);
  or d (d_out, z_out, u_out);
  or or_1 (or_1_out, d_out, y_out, v_out);
  or f (f_out, c_out, z_out, decoder_1_out2);
  or g (g_out, f_out, v_out, decoder_1_out4);
  or e (e_out, or_1_out, decoder_1_out0);
  _7_Segment_Display u_7_segment_display_1 (
    .g(g_out), .f(f_out), .a(a_out), .b(b_out), .e(e_out), .d(d_out), .c(c_out), .dp(decoder_1_out12));

  // Notes on the sheet:
  //   1
  //   2
  //   8
  //   3
  //   4
  //   5
  //   1
  //   2
  //   4
  //   5
  //   9
  //   10
  //   9
  //   6
  //   3
  //   6
  //   8
  //   12
  //   13
  //   1
  //   2
  //   4
  //   5
  //   9
  //   10
  //   11
  //   12
  //   13
  //   1
  //   2
  //   8
  //   3
  //   4
  //   5
  //   h
  //   11
  //   3
  //   6
  //   8
  //   10
  //   12
  //   13
  //   9
  //   6
  //   11
  //   g f a b
  //   e d c h
endmodule
