// Logisim project Decoder.circ as structural Verilog: 1 circuit, main circuit main
module main (
  input  [3:0] in_1
);

  wire a_out, b_out, c_out, d_out, decoder_1_out0, decoder_1_out1, decoder_1_out2, decoder_1_out3,
       decoder_1_out4, decoder_1_out5, decoder_1_out6, decoder_1_out7, decoder_1_out8, decoder_1_out9,
       decoder_1_out10, decoder_1_out11, decoder_1_out12, decoder_1_out13, decoder_1_out14, decoder_1_out15,
       e_out, f_out, g_out, not_1_out, not_2_out, not_3_out, or_1_out;

  Decoder #(.select(4)) decoder_1 (
    .out0(decoder_1_out0), .out1(decoder_1_out1), .out2(decoder_1_out2), .out3(decoder_1_out3),
    .out4(decoder_1_out4), .out5(decoder_1_out5), .out6(decoder_1_out6), .out7(decoder_1_out7),
    .out8(decoder_1_out8), .out9(decoder_1_out9), .out10(decoder_1_out10), .out11(decoder_1_out11),
    .out12(decoder_1_out12), .out13(decoder_1_out13), .out14(decoder_1_out14), .out15(decoder_1_out15),
    .sel(in_1), .en(1'b1));
  or or_1 (or_1_out, decoder_1_out15, decoder_1_out14, decoder_1_out13);
  or a (a_out, decoder_1_out0, decoder_1_out3, decoder_1_out5, decoder_1_out7, decoder_1_out10);
  or b (b_out, decoder_1_out0, decoder_1_out3, decoder_1_out5, decoder_1_out10);
  or c (c_out, decoder_1_out0, decoder_1_out1, decoder_1_out3, decoder_1_out5, decoder_1_out8, decoder_1_out9);
  or d (d_out, decoder_1_out2, decoder_1_out5, decoder_1_out7, decoder_1_out10);
  or e (e_out, decoder_1_out3, decoder_1_out4, decoder_1_out12, or_1_out);
  or f (f_out, decoder_1_out4, decoder_1_out6, or_1_out, decoder_1_out11, decoder_1_out12);
  or g (g_out, or_1_out, decoder_1_out12);
  not not_1 (not_1_out, e_out);
  not not_2 (not_2_out, f_out);
  not not_3 (not_3_out, g_out);
  _7_Segment_Display u_7_segment_display_1 (
    .g(not_3_out), .f(not_2_out), .a(a_out), .b(b_out), .e(not_1_out), .d(d_out), .c(c_out),
    .dp(decoder_1_out12));

  // Notes on the sheet:
  //   g f a b
  //   e d c h
endmodule
