// Logisim project Boolean Algebra.circ as structural Verilog: 1 circuit, main circuit main
module main (
  input  A,
  input  B,
  input  C,
  input  D
);

  wire a_out, and_1_out, and_2_out, and_3_out, and_4_out, and_5_out, and_6_out, and_7_out, and_8_out,
       and_9_out, and_10_out, and_11_out, and_12_out, and_13_out, and_14_out, b_out, c_out, d_out, e_out,
       f_out, g_out, h_out, not_1_out, not_2_out, not_3_out, not_4_out, not_5_out, not_6_out, or_1_out,
       or_2_out, or_3_out, xnor_1_out, xnor_2_out, xnor_3_out, xnor_4_out;

  not not_1 (not_1_out, A);
  not not_2 (not_2_out, B);
  not not_3 (not_3_out, C);
  not not_4 (not_4_out, D);
  and and_1 (and_1_out, not_1_out, C, D);
  xnor xnor_1 (xnor_1_out, B, D);
  xnor xnor_2 (xnor_2_out, A, C);
  and and_2 (and_2_out, not_1_out, not_2_out);
  xnor xnor_3 (xnor_3_out, C, D);
  xnor xnor_4 (xnor_4_out, not_2_out, C);
  and and_3 (and_3_out, not_2_out, not_3_out);
  and and_4 (and_4_out, not_2_out, C, not_4_out);
  and and_5 (and_5_out, not_1_out, B, D);
  and and_6 (and_6_out, C, D);
  and and_7 (and_7_out, A, C);
  not not_5 (not_5_out, and_7_out);
  and and_8 (and_8_out, xnor_1_out, not_3_out, not_1_out);
  and and_9 (and_9_out, xnor_2_out, not_2_out, not_4_out);
  and and_10 (and_10_out, and_2_out, xnor_3_out);
  and and_11 (and_11_out, xnor_4_out, not_1_out, D);
  and and_12 (and_12_out, and_6_out, not_2_out, not_1_out);
  and and_13 (and_13_out, B, not_3_out, not_4_out);
  and and_14 (and_14_out, not_5_out, B, not_4_out);
  or or_1 (or_1_out, not_4_out, or_2_out);
  or or_2 (or_2_out, not_3_out, B, not_1_out);
  or or_3 (or_3_out, and_12_out, and_13_out);
  not not_6 (not_6_out, and_14_out);
  and h (h_out, and_13_out, A);
  or u_a (a_out, and_1_out, and_8_out, and_9_out);
  or u_b (b_out, and_8_out, and_9_out, and_10_out);
  or u_c (c_out, and_11_out, and_3_out);
  or u_d (d_out, and_4_out, and_5_out);
  not e (e_out, or_3_out);
  and f (f_out, not_6_out, or_1_out);
  not g (g_out, h_out);
  _7_Segment_Display u_7_segment_display_1 (
    .g(g_out), .f(f_out), .a(a_out), .b(b_out), .e(e_out), .d(d_out), .c(c_out), .dp(h_out));

  // Notes on the sheet:
  //   9x 3-Input AND Gate: 3x 4073 3-Input AND IC
  //   3x 3-Input OR Gate: 1x 4075 3-Input OR IC
  //   7x 2-Input AND Gate: 2x 7404 2-Input AND IC
  //   4x 2-Input OR Gate: 1x7432 OR IC
  //   4x 2-Input XNOR Gate: 1x4077 XNOR IC
  //   8x NOT Gate: 1x7404 NOT IC
  //   Boolean Algebra
  //   Group: 05
  //   g f a b
  //   e d c h
endmodule
