// Logisim project K-Map.circ as structural Verilog: 1 circuit, main circuit main
module main (
  input  A,
  input  B,
  input  C,
  input  D
);

  wire a_out, A_prime_B_prime_C_prime_D_prime_out, A_prime_B_prime_CD_out, A_prime_B_prime_D_out,
       A_prime_CD_out, A_prime_D_out, AB_h_out, AB_prime_out, ACD_prime_out, b_out, B_prime_C_prime_out,
       B_prime_CD_prime_out, B_prime_D_prime_out, BC_prime_D_out, BD_out, c_out, C_prime_D_out, CD_prime_out,
       d_out, e_out, f_out, g_out, not_1_out, not_2_out, not_3_out, not_4_out, or_1_out;

  not not_1 (not_1_out, A);
  not not_2 (not_2_out, B);
  not not_3 (not_3_out, D);
  not not_4 (not_4_out, C);
  and AB_h (AB_h_out, A, B);
  and BD (BD_out, B, D);
  and A_prime_B_prime_D (A_prime_B_prime_D_out, not_1_out, not_2_out, D);
  and B_prime_C_prime (B_prime_C_prime_out, not_2_out, not_4_out);
  and C_prime_D (C_prime_D_out, not_4_out, D);
  and AB_prime (AB_prime_out, A, not_2_out);
  and CD_prime (CD_prime_out, C, not_3_out);
  and B_prime_D_prime (B_prime_D_prime_out, not_2_out, not_3_out);
  and A_prime_D (A_prime_D_out, not_1_out, D);
  and BC_prime_D (BC_prime_D_out, BD_out, not_4_out);
  and A_prime_B_prime_CD (A_prime_B_prime_CD_out, A_prime_B_prime_D_out, C);
  and A_prime_B_prime_C_prime_D_prime (A_prime_B_prime_C_prime_D_prime_out, B_prime_C_prime_out, not_1_out, not_3_out);
  and ACD_prime (ACD_prime_out, CD_prime_out, A);
  and B_prime_CD_prime (B_prime_CD_prime_out, B_prime_D_prime_out, C);
  and A_prime_CD (A_prime_CD_out, A_prime_D_out, C);
  or or_1 (or_1_out, A_prime_B_prime_C_prime_D_prime_out, ACD_prime_out);
  or u_a (a_out, BD_out, or_1_out, A_prime_CD_out);
  or u_b (b_out, BC_prime_D_out, A_prime_B_prime_CD_out, or_1_out);
  or u_c (c_out, B_prime_C_prime_out, C_prime_D_out, A_prime_B_prime_D_out);
  or u_d (d_out, BD_out, B_prime_CD_prime_out);
  or e (e_out, B_prime_C_prime_out, AB_prime_out, CD_prime_out, BD_out);
  or f (f_out, B_prime_C_prime_out, B_prime_D_prime_out, A_prime_D_out);
  or g (g_out, not_1_out, not_2_out);
  _7_Segment_Display u_7_segment_display_1 (
    .g(g_out), .f(f_out), .a(a_out), .b(b_out), .e(e_out), .d(d_out), .c(c_out), .dp(AB_h_out));

  // Notes on the sheet:
  //   K-Map
  //   Grouo: 05
  //   g f a b
  //   e d c h
endmodule
