// Logisim project MUX.circ as structural Verilog: 1 circuit, main circuit main
module main (
  input  A,
  input  [2:0] S,
  input  in_3,
  input  in_4
);

  wire multiplexer_1_out, multiplexer_2_out, multiplexer_3_out, multiplexer_4_out, multiplexer_5_out,
       multiplexer_6_out, multiplexer_7_out, not_1_out, not_2_out;

  not not_1 (not_1_out, A);
  Multiplexer #(.select(3)) multiplexer_1 (
    .in0(not_1_out), .in1(in_4), .in2(A), .in3(not_1_out), .in4(in_4), .in5(not_1_out), .in6(in_4),
    .in7(not_1_out), .out(multiplexer_1_out), .sel(S), .en(in_3));
  Multiplexer #(.select(3)) multiplexer_2 (
    .in0(not_1_out), .in1(in_4), .in2(A), .in3(not_1_out), .in4(in_4), .in5(not_1_out), .in6(in_4),
    .in7(in_4), .out(multiplexer_2_out), .sel(S), .en(in_3));
  Multiplexer #(.select(3)) multiplexer_3 (
    .in0(in_3), .in1(in_3), .in2(in_4), .in3(not_1_out), .in4(in_4), .in5(not_1_out), .in6(in_4), .in7(in_4),
    .out(multiplexer_3_out), .sel(S), .en(in_3));
  Multiplexer #(.select(3)) multiplexer_4 (
    .in0(in_4), .in1(in_4), .in2(in_3), .in3(in_4), .in4(in_4), .in5(not_1_out), .in6(in_4), .in7(not_1_out),
    .out(multiplexer_4_out), .sel(S), .en(in_3));
  _7_Segment_Display u_7_segment_display_1 (
    .g(multiplexer_7_out), .f(multiplexer_6_out), .a(multiplexer_1_out), .b(multiplexer_2_out),
    .e(multiplexer_5_out), .d(multiplexer_4_out), .c(multiplexer_3_out), .dp(not_2_out));
  Multiplexer #(.select(3)) multiplexer_5 (
    .in0(in_3), .in1(in_3), .in2(in_3), .in3(A), .in4(in_4), .in5(not_1_out), .in6(not_1_out),
    .in7(not_1_out), .out(multiplexer_5_out), .sel(S), .en(in_3));
  Multiplexer #(.select(3)) multiplexer_6 (
    .in0(in_3), .in1(in_3), .in2(in_3), .in3(not_1_out), .in4(in_4), .in5(not_1_out), .in6(in_4),
    .in7(not_1_out), .out(multiplexer_6_out), .sel(S), .en(in_3));
  Multiplexer #(.select(3)) multiplexer_7 (
    .in0(in_3), .in1(in_3), .in2(in_3), .in3(in_3), .in4(not_1_out), .in5(not_1_out), .in6(not_1_out),
    .in7(not_1_out), .out(multiplexer_7_out), .sel(S), .en(in_3));
  not not_2 (not_2_out, multiplexer_7_out);

  // Notes on the sheet:
  //   a
  //   b
  //   c
  //   d
  //   g f a b
  //   e d c h
  //   e
  //   f
  //   MUX
  //   Group: 05
  //   g
  //   h
endmodule
