// Logisim project NAND.circ as structural Verilog: 1 circuit, main circuit main
module main (
  input  A,
  input  B,
  input  C,
  input  D
);

  wire a_out, b_out, c_out, d_out, e_out, f_out, g_out, h_out, nand_1_out, nand_2_out, nand_3_out,
       nand_4_out, nand_5_out, nand_6_out, nand_7_out, nand_8_out, nand_9_out, nand_10_out, nand_11_out,
       nand_12_out, nand_13_out, nand_14_out, nand_15_out, nand_16_out, nand_17_out, nand_18_out,
       nand_19_out, nand_20_out, nand_21_out, nand_22_out, nand_23_out, nand_24_out, nand_25_out,
       nand_26_out, nand_27_out, nand_28_out, nand_29_out, nand_30_out, nand_31_out, nand_32_out,
       nand_33_out, nand_34_out, nand_35_out, nand_36_out, nand_37_out, nand_38_out, nand_39_out,
       nand_40_out, nand_41_out, nand_42_out, nand_43_out;

  nand nand_1 (nand_1_out, A, A);
  nand nand_2 (nand_2_out, B, B);
  nand nand_3 (nand_3_out, C, C);
  nand nand_4 (nand_4_out, D, D);
  nand nand_5 (nand_5_out, nand_1_out, nand_2_out);
  nand nand_6 (nand_6_out, C, D);
  nand nand_7 (nand_7_out, B, D);
  nand nand_8 (nand_8_out, C, nand_4_out);
  nand nand_9 (nand_9_out, nand_3_out, D);
  nand nand_10 (nand_10_out, nand_2_out, nand_3_out);
  nand nand_11 (nand_11_out, nand_5_out, nand_5_out);
  nand nand_12 (nand_12_out, nand_6_out, nand_6_out);
  nand nand_13 (nand_13_out, nand_8_out, nand_8_out);
  nand nand_14 (nand_14_out, nand_9_out, nand_9_out);
  nand nand_15 (nand_15_out, nand_9_out, nand_10_out);
  nand nand_16 (nand_16_out, nand_2_out, nand_4_out);
  nand nand_17 (nand_17_out, nand_16_out, nand_16_out);
  nand nand_18 (nand_18_out, nand_10_out, nand_8_out);
  nand nand_19 (nand_19_out, A, nand_2_out);
  nand nand_20 (nand_20_out, nand_10_out, nand_16_out);
  nand nand_21 (nand_21_out, nand_1_out, D);
  nand g (g_out, A, B);
  nand nand_22 (nand_22_out, nand_23_out, nand_23_out);
  nand nand_23 (nand_23_out, nand_11_out, nand_3_out);
  nand nand_24 (nand_24_out, nand_12_out, nand_1_out);
  nand nand_25 (nand_25_out, nand_13_out, A);
  nand nand_26 (nand_26_out, nand_11_out, nand_12_out);
  nand nand_27 (nand_27_out, nand_14_out, B);
  nand nand_28 (nand_28_out, nand_15_out, nand_15_out);
  nand nand_29 (nand_29_out, nand_17_out, C);
  nand nand_30 (nand_30_out, nand_18_out, nand_18_out);
  nand nand_31 (nand_31_out, nand_20_out, nand_20_out);
  nand h (h_out, g_out, g_out);
  nand nand_32 (nand_32_out, nand_22_out, nand_4_out);
  nand nand_33 (nand_33_out, nand_11_out, D);
  nand u_d (d_out, nand_7_out, nand_29_out);
  nand nand_34 (nand_34_out, nand_7_out, nand_30_out);
  nand f (f_out, nand_31_out, nand_21_out);
  nand nand_35 (nand_35_out, nand_32_out, nand_24_out);
  nand u_c (c_out, nand_33_out, nand_28_out);
  nand nand_36 (nand_36_out, nand_34_out, nand_34_out);
  nand nand_37 (nand_37_out, nand_35_out, nand_35_out);
  nand nand_38 (nand_38_out, nand_39_out, nand_39_out);
  nand nand_39 (nand_39_out, nand_32_out, nand_26_out);
  nand e (e_out, nand_36_out, nand_19_out);
  nand nand_40 (nand_40_out, nand_37_out, nand_7_out);
  nand nand_41 (nand_41_out, nand_38_out, nand_27_out);
  nand nand_42 (nand_42_out, nand_40_out, nand_40_out);
  nand nand_43 (nand_43_out, nand_41_out, nand_41_out);
  nand u_a (a_out, nand_42_out, nand_25_out);
  nand u_b (b_out, nand_25_out, nand_43_out);
  _7_Segment_Display u_7_segment_display_1 (
    .g(g_out), .f(f_out), .a(a_out), .b(b_out), .e(e_out), .d(d_out), .c(c_out), .dp(h_out));

  // Notes on the sheet:
  //   52x 2 Input NAND Gate: 13x 7400 2-Input NAND IC
  //   NAND
  //   Group: 05
  //   g f a b
  //   e d c h
endmodule
