// Logisim project POS.circ as structural Verilog: 1 circuit, main circuit main
module main (
  input  A,
  input  B,
  input  C,
  input  D
);

  wire _0_out, _1_out, _2_out, _3_out, _4_out, _5_out, _6_out, _7_out, _8_out, _9_out, _10_out, _11_out,
       _12_out, a_out, b_out, c_out, d_out, e_out, f_out, h_out, m_out, not_1_out, not_2_out, not_3_out,
       not_4_out, u_out, v_out, w_out, x_out, y_out, z_out;

  not not_1 (not_1_out, A);
  not not_2 (not_2_out, B);
  not not_3 (not_3_out, C);
  not not_4 (not_4_out, D);
  or _0 (_0_out, A, B, C, D);
  or _1 (_1_out, A, B, C, not_4_out);
  or _2 (_2_out, A, B, not_3_out, D);
  or _3 (_3_out, A, B, not_3_out, not_4_out);
  or _4 (_4_out, A, not_2_out, C, D);
  or _5 (_5_out, A, not_2_out, C, not_4_out);
  or _6 (_6_out, A, not_2_out, not_3_out, D);
  or _8 (_8_out, not_1_out, B, C, D);
  or _7 (_7_out, A, not_2_out, not_3_out, not_4_out);
  or _9 (_9_out, not_1_out, B, C, not_4_out);
  or _10 (_10_out, not_1_out, B, not_3_out, D);
  or _11 (_11_out, not_1_out, B, not_3_out, not_4_out);
  or _12 (_12_out, not_1_out, not_2_out, C, D);
  and x (x_out, _4_out, _6_out);
  and y (y_out, _11_out, _12_out);
  and z (z_out, _8_out, _9_out);
  and u (u_out, z_out, _1_out);
  and v (v_out, x_out, _2_out);
  and w (w_out, _7_out, _10_out);
  and m (m_out, _0_out, _3_out);
  and u_a (a_out, y_out, u_out, v_out);
  and u_b (b_out, a_out, _7_out);
  and u_c (c_out, v_out, y_out, w_out);
  and u_d (d_out, m_out, u_out, f_out);
  and e (e_out, _3_out, _4_out, _12_out);
  and f (f_out, x_out, y_out);
  and h (h_out, m_out, u_out, v_out, _5_out, w_out, _11_out);
  _7_Segment_Display u_7_segment_display_1 (
    .g(_12_out), .f(f_out), .a(a_out), .b(b_out), .e(e_out), .d(d_out), .c(c_out), .dp(h_out));

  // Notes on the sheet:
  //   g
  //   POS
  //   Group: 05
  //   g f a b
  //   e d c h
endmodule
