// Logisim project SOP.circ as structural Verilog: 1 circuit, main circuit main
module main (
  input  A,
  input  B,
  input  C,
  input  D
);

  wire _0_out, _1_out, _2_out, _3_out, _4_out, _5_out, _6_out, _7_out, _8_out, _9_out, _10_out, _11_out,
       _12_out, a_out, b_out, c_out, d_out, e_out, f_out, g_out, not_1_out, not_2_out, not_3_out, not_4_out,
       u_out, v_out, x_out, y_out, z_out;

  not not_1 (not_1_out, A);
  not not_2 (not_2_out, B);
  not not_3 (not_3_out, C);
  not not_4 (not_4_out, D);
  and _0 (_0_out, not_1_out, not_2_out, not_3_out, not_4_out);
  and _1 (_1_out, not_1_out, not_2_out, not_3_out, D);
  and _2 (_2_out, not_1_out, not_2_out, C, not_4_out);
  and _3 (_3_out, not_1_out, not_2_out, C, D);
  and _4 (_4_out, not_1_out, B, not_3_out, not_4_out);
  and _5 (_5_out, not_1_out, B, not_3_out, D);
  and _7 (_7_out, not_1_out, B, C, D);
  and _6 (_6_out, not_1_out, B, C, not_4_out);
  and _8 (_8_out, A, not_2_out, not_3_out, not_4_out);
  and _9 (_9_out, A, not_2_out, not_3_out, D);
  and _10 (_10_out, A, not_2_out, C, not_4_out);
  and _11 (_11_out, A, not_2_out, C, D);
  and _12 (_12_out, A, B, not_3_out, not_4_out);
  or x (x_out, _0_out, _3_out, _5_out);
  or y (y_out, _1_out, _8_out, _9_out);
  or z (z_out, _7_out, _10_out);
  or u (u_out, _2_out, _5_out);
  or v (v_out, _6_out, _11_out);
  or u_a (a_out, x_out, z_out);
  or u_b (b_out, x_out, _10_out);
  or u_c (c_out, x_out, y_out);
  or u_d (d_out, z_out, u_out);
  or e (e_out, d_out, y_out, v_out, _0_out);
  or f (f_out, c_out, z_out, _2_out);
  or g (g_out, f_out, v_out, _4_out);
  _7_Segment_Display u_7_segment_display_1 (
    .g(g_out), .f(f_out), .a(a_out), .b(b_out), .e(e_out), .d(d_out), .c(c_out), .dp(_12_out));

  // Notes on the sheet:
  //   h
  //   SOP
  //   Group: 05
  //   g f a b
  //   e d c h
endmodule
