// Logisim project Sequential Part Logisim - J-K Flip Flop.circ as structural Verilog: 1 circuit, main circuit main
module main (
);

  wire a_out, and_1_out, and_2_out, and_3_out, and_4_out, and_5_out, and_6_out, and_7_out, and_8_out, b_out,
       c_out, clock_1_out, d_out, decoder_1_out0, decoder_1_out1, decoder_1_out2, decoder_1_out3,
       decoder_1_out4, decoder_1_out5, decoder_1_out6, decoder_1_out7, decoder_1_out8, decoder_1_out9,
       decoder_1_out10, decoder_1_out11, decoder_1_out12, decoder_1_out13, decoder_1_out14, decoder_1_out15,
       e_out, f_out, g_out, j_k_ff_1_qn, j_k_ff_2_qn, j_k_ff_3_qn, j_k_ff_4_qn, not_1_out, not_2_out,
       not_3_out, not_4_out, not_5_out, not_6_out, not_8_out, not_9_out, not_10_out, not_11_out, not_12_out,
       not_13_out, not_14_out, or_1_out, or_2_out, or_3_out, u_out, v_out, x_out, y_out, z_out;
  wire [3:0] j_k_ff_1_q;

  Decoder #(.select(4)) decoder_1 (
    .out0(decoder_1_out0), .out1(decoder_1_out1), .out2(decoder_1_out2), .out3(decoder_1_out3),
    .out4(decoder_1_out4), .out5(decoder_1_out5), .out6(decoder_1_out6), .out7(decoder_1_out7),
    .out8(decoder_1_out8), .out9(decoder_1_out9), .out10(decoder_1_out10), .out11(decoder_1_out11),
    .out12(decoder_1_out12), .out13(decoder_1_out13), .out14(decoder_1_out14), .out15(decoder_1_out15),
    .sel(j_k_ff_1_q), .en(1'b1));
  not not_1 (not_1_out, decoder_1_out1);
  not not_2 (not_2_out, decoder_1_out5);
  not not_3 (not_3_out, decoder_1_out0);
  not not_4 (not_4_out, decoder_1_out4);
  not not_5 (not_5_out, decoder_1_out3);
  not not_6 (not_6_out, decoder_1_out2);
  // NOT_Gate not_7 has open pins: in=decoder_1_out13, out=open
  not not_8 (not_8_out, decoder_1_out6);
  not not_9 (not_9_out, decoder_1_out9);
  not not_10 (not_10_out, decoder_1_out12);
  not not_11 (not_11_out, decoder_1_out10);
  not not_12 (not_12_out, decoder_1_out7);
  not not_13 (not_13_out, decoder_1_out11);
  not not_14 (not_14_out, decoder_1_out8);
  // NOT_Gate not_15 has open pins: in=decoder_1_out15, out=open
  // NOT_Gate not_16 has open pins: in=decoder_1_out14, out=open
  and x (x_out, not_3_out, not_5_out, not_2_out);
  and y (y_out, not_1_out, not_14_out, not_9_out);
  and z (z_out, not_12_out, not_11_out);
  and u (u_out, not_6_out, not_2_out);
  and v (v_out, not_8_out, not_13_out);
  and a (a_out, x_out, z_out);
  and b (b_out, x_out, not_11_out);
  and c (c_out, x_out, y_out);
  and d (d_out, z_out, u_out);
  and e (e_out, d_out, y_out, v_out, not_3_out);
  and f (f_out, c_out, z_out, not_6_out);
  and g (g_out, f_out, v_out, not_4_out);
  _7_Segment_Display #(.active("false")) u_7_segment_display_1 (
    .g(g_out), .f(f_out), .a(a_out), .b(b_out), .e(e_out), .d(d_out), .c(c_out), .dp(not_10_out));
  Clock clock_1 (.out(clock_1_out));
  or or_1 (or_1_out, j_k_ff_4_qn, j_k_ff_3_qn);
  J_K_Flip_Flop j_k_ff_1 (
    .J(or_1_out), .clk(clock_1_out), .K(or_1_out), .Q(j_k_ff_1_q[0]), .Qn(j_k_ff_1_qn));  // open: preset, en, reset
  and and_1 (and_1_out, j_k_ff_4_qn, j_k_ff_1_q[0]);
  and and_2 (and_2_out, j_k_ff_1_q[0], j_k_ff_3_qn);
  and and_3 (and_3_out, j_k_ff_1_qn, j_k_ff_1_q[3]);
  or or_2 (or_2_out, and_1_out, and_2_out);
  J_K_Flip_Flop j_k_ff_2 (
    .J(or_2_out), .clk(clock_1_out), .K(or_2_out), .Q(j_k_ff_1_q[1]), .Qn(j_k_ff_2_qn));  // open: preset, en, reset
  and and_4 (and_4_out, j_k_ff_2_qn, and_3_out);
  and and_5 (and_5_out, and_1_out, j_k_ff_1_q[1]);
  and and_6 (and_6_out, and_2_out, j_k_ff_1_q[1]);
  or or_3 (or_3_out, and_5_out, and_4_out);
  and and_7 (and_7_out, and_5_out, j_k_ff_1_q[2]);
  J_K_Flip_Flop j_k_ff_3 (
    .J(and_6_out), .clk(clock_1_out), .K(or_3_out), .Q(j_k_ff_1_q[2]), .Qn(j_k_ff_3_qn));  // open: preset, en, reset
  and and_8 (and_8_out, j_k_ff_1_q[2], j_k_ff_2_qn, j_k_ff_1_qn);
  J_K_Flip_Flop j_k_ff_4 (
    .J(and_7_out), .clk(clock_1_out), .K(and_8_out), .Q(j_k_ff_1_q[3]), .Qn(j_k_ff_4_qn));  // open: preset, en, reset

  // Notes on the sheet:
  //   IC 74154
  //   Group: 05
  //   h
  //   Text: Anta-BrEnner. 
  //   Ignore the NOT Gate
  //   Most Efficient and Cost Effective
  //   It is used for making the decoder active Low
  //   g f a b
  //   e d c h
  //   J-K Flip Flop
endmodule
