// Logisim project Sequential Part Logisim - T Flip Flop.circ as structural Verilog: 1 circuit, main circuit main
module main (
);

  wire a_out, b_out, c_out, clock_1_out, d_out, decoder_1_out0, decoder_1_out1, decoder_1_out2,
       decoder_1_out3, decoder_1_out4, decoder_1_out5, decoder_1_out6, decoder_1_out7, decoder_1_out8,
       decoder_1_out9, decoder_1_out10, decoder_1_out11, decoder_1_out12, decoder_1_out13, decoder_1_out14,
       decoder_1_out15, e_out, f_out, g_out, not_1_out, not_2_out, not_3_out, not_4_out, not_5_out,
       not_6_out, not_7_out, not_8_out, not_9_out, not_10_out, not_11_out, not_12_out, not_13_out, u_out,
       v_out, x_out, y_out, z_out;
  wire [3:0] t_ff_1_q;

  Clock clock_1 (.out(clock_1_out));
  Decoder #(.select(4)) decoder_1 (
    .out0(decoder_1_out0), .out1(decoder_1_out1), .out2(decoder_1_out2), .out3(decoder_1_out3),
    .out4(decoder_1_out4), .out5(decoder_1_out5), .out6(decoder_1_out6), .out7(decoder_1_out7),
    .out8(decoder_1_out8), .out9(decoder_1_out9), .out10(decoder_1_out10), .out11(decoder_1_out11),
    .out12(decoder_1_out12), .out13(decoder_1_out13), .out14(decoder_1_out14), .out15(decoder_1_out15),
    .sel(t_ff_1_q), .en(1'b1));
  not not_1 (not_1_out, decoder_1_out1);
  not not_2 (not_2_out, decoder_1_out4);
  not not_3 (not_3_out, decoder_1_out5);
  not not_4 (not_4_out, decoder_1_out2);
  not not_5 (not_5_out, decoder_1_out3);
  not not_6 (not_6_out, decoder_1_out0);
  T_Flip_Flop #(.trigger("falling")) t_ff_1 (
    .clk(clock_1_out), .T(1'b1), .Q(t_ff_1_q[0]));  // open: Qn, preset, reset, en
  T_Flip_Flop #(.trigger("falling")) t_ff_2 (
    .clk(t_ff_1_q[0]), .T(1'b1), .Q(t_ff_1_q[1]));  // open: Qn, preset, reset, en
  not not_7 (not_7_out, decoder_1_out7);
  not not_8 (not_8_out, decoder_1_out11);
  not not_9 (not_9_out, decoder_1_out8);
  not not_10 (not_10_out, decoder_1_out6);
  not not_11 (not_11_out, decoder_1_out12);
  not not_12 (not_12_out, decoder_1_out10);
  not not_13 (not_13_out, decoder_1_out9);
  // NOT_Gate not_14 has open pins: in=decoder_1_out13, out=open
  T_Flip_Flop #(.trigger("falling")) t_ff_3 (
    .clk(t_ff_1_q[1]), .T(1'b1), .Q(t_ff_1_q[2]));  // open: Qn, preset, reset, en
  // NOT_Gate not_15 has open pins: in=decoder_1_out14, out=open
  // NOT_Gate not_16 has open pins: in=decoder_1_out15, out=open
  T_Flip_Flop #(.trigger("falling")) t_ff_4 (
    .clk(t_ff_1_q[2]), .T(1'b1), .Q(t_ff_1_q[3]));  // open: Qn, preset, reset, en
  and x (x_out, not_6_out, not_5_out, not_3_out);
  and y (y_out, not_1_out, not_9_out, not_13_out);
  and z (z_out, not_7_out, not_12_out);
  and u (u_out, not_4_out, not_3_out);
  and v (v_out, not_10_out, not_8_out);
  and a (a_out, x_out, z_out);
  and b (b_out, x_out, not_12_out);
  and c (c_out, x_out, y_out);
  and d (d_out, z_out, u_out);
  and e (e_out, d_out, y_out, v_out, not_6_out);
  and f (f_out, c_out, z_out, not_4_out);
  and g (g_out, f_out, v_out, not_2_out);
  _7_Segment_Display #(.active("false")) u_7_segment_display_1 (
    .g(g_out), .f(f_out), .a(a_out), .b(b_out), .e(e_out), .d(d_out), .c(c_out), .dp(not_11_out));

  // Notes on the sheet:
  //   IC 74154
  //   Group: 05
  //   T Flip-Flop
  //   h
  //   Text: Anta-BrEnner. 
  //   Please ignore the NOT Gate
  //   It is used for making the decoder active Low
  //   Most Efficient and Cost Effective
  //   g f a b
  //   e d c h
endmodule
