// Logisim project NOR - Copy.circ as structural Verilog: 1 circuit, main circuit main
module main (
  input  A,
  input  B,
  input  C,
  input  D
);

  wire nor_1_out, nor_2_out, nor_3_out, nor_4_out, nor_5_out, nor_6_out, nor_7_out, nor_8_out, nor_9_out,
       nor_10_out, nor_11_out, nor_12_out, nor_13_out, nor_14_out, nor_15_out, nor_16_out, nor_17_out,
       nor_18_out, nor_19_out, nor_20_out, nor_21_out, nor_22_out, nor_23_out, nor_24_out, nor_25_out,
       nor_26_out, nor_27_out, nor_28_out, nor_29_out, nor_30_out, nor_31_out, nor_32_out, nor_33_out,
       nor_34_out, nor_35_out, nor_36_out, nor_37_out, nor_38_out, nor_39_out, nor_40_out, nor_41_out,
       nor_42_out, nor_43_out, nor_44_out, nor_45_out, nor_46_out, nor_47_out, nor_48_out, nor_49_out,
       nor_50_out, nor_51_out, nor_52_out, nor_53_out, nor_54_out, nor_55_out, nor_56_out, nor_57_out,
       nor_58_out, nor_59_out, nor_60_out;

  nor nor_1 (nor_1_out, A, A);
  nor nor_2 (nor_2_out, B, B);
  nor nor_3 (nor_3_out, C, C);
  nor nor_4 (nor_4_out, D, D);
  nor nor_5 (nor_5_out, A, B);
  nor nor_6 (nor_6_out, A, nor_3_out);
  nor nor_7 (nor_7_out, nor_2_out, nor_4_out);
  nor nor_8 (nor_8_out, nor_3_out, D);
  nor nor_9 (nor_9_out, nor_2_out, C);
  nor nor_10 (nor_10_out, B, C);
  nor nor_11 (nor_11_out, C, nor_4_out);
  nor nor_12 (nor_12_out, nor_20_out, B);
  nor nor_13 (nor_13_out, nor_2_out, nor_4_out);
  nor nor_14 (nor_14_out, nor_1_out, B);
  nor nor_15 (nor_15_out, B, D);
  nor nor_16 (nor_16_out, A, nor_4_out);
  nor nor_17 (nor_17_out, nor_1_out, nor_2_out);
  nor nor_18 (nor_18_out, nor_5_out, nor_5_out);
  nor nor_19 (nor_19_out, nor_6_out, nor_6_out);
  nor nor_20 (nor_20_out, nor_8_out, nor_8_out);
  nor nor_21 (nor_21_out, nor_18_out, nor_3_out);
  nor nor_22 (nor_22_out, nor_9_out, nor_9_out);
  nor nor_23 (nor_23_out, nor_18_out, nor_4_out);
  nor nor_24 (nor_24_out, nor_12_out, nor_13_out);
  nor nor_25 (nor_25_out, nor_15_out, nor_16_out);
  nor nor_26 (nor_26_out, nor_17_out, nor_17_out);
  nor nor_27 (nor_27_out, nor_18_out, C);
  nor nor_28 (nor_28_out, nor_19_out, nor_4_out);
  nor nor_29 (nor_29_out, nor_20_out, nor_1_out);
  nor nor_30 (nor_30_out, nor_21_out, nor_21_out);
  nor nor_31 (nor_31_out, nor_22_out, nor_4_out);
  nor nor_32 (nor_32_out, nor_10_out, nor_11_out);
  nor nor_33 (nor_33_out, nor_24_out, nor_24_out);
  nor nor_34 (nor_34_out, nor_14_out, nor_10_out);
  nor nor_35 (nor_35_out, nor_25_out, nor_25_out);
  nor nor_36 (nor_36_out, nor_27_out, nor_27_out);
  nor nor_37 (nor_37_out, nor_30_out, nor_4_out);
  nor nor_38 (nor_38_out, nor_32_out, nor_32_out);
  nor nor_39 (nor_39_out, nor_40_out, nor_8_out);
  nor nor_40 (nor_40_out, nor_34_out, nor_34_out);
  nor nor_41 (nor_41_out, nor_10_out, nor_35_out);
  nor nor_42 (nor_42_out, nor_36_out, D);
  nor nor_43 (nor_43_out, nor_42_out, nor_37_out);
  nor nor_44 (nor_44_out, nor_43_out, nor_43_out);
  nor nor_45 (nor_45_out, nor_46_out, nor_46_out);
  nor nor_46 (nor_46_out, nor_38_out, nor_23_out);
  nor nor_47 (nor_47_out, nor_39_out, nor_39_out);
  nor nor_48 (nor_48_out, nor_41_out, nor_41_out);
  nor nor_49 (nor_49_out, nor_42_out, nor_28_out);
  nor nor_50 (nor_50_out, nor_49_out, nor_49_out);
  nor nor_51 (nor_51_out, nor_44_out, nor_31_out);
  nor nor_52 (nor_52_out, nor_47_out, nor_7_out);
  nor nor_53 (nor_53_out, nor_50_out, nor_7_out);
  nor nor_54 (nor_54_out, nor_51_out, nor_51_out);
  nor nor_55 (nor_55_out, nor_52_out, nor_52_out);
  nor nor_56 (nor_56_out, nor_53_out, nor_53_out);
  nor nor_57 (nor_57_out, nor_54_out, nor_28_out);
  nor nor_58 (nor_58_out, nor_56_out, nor_29_out);
  nor nor_59 (nor_59_out, nor_57_out, nor_57_out);
  nor nor_60 (nor_60_out, nor_58_out, nor_58_out);
  _7_Segment_Display u_7_segment_display_1 (
    .g(nor_26_out), .f(nor_48_out), .a(nor_60_out), .b(nor_59_out), .e(nor_55_out), .d(nor_33_out),
    .c(nor_45_out), .dp(nor_17_out));

  // Notes on the sheet:
  //   60x NOR Gate: 15x 7402 NOR IC
  //   NOR
  //   Group: 05
  //   g f a b
  //   e d c h
endmodule
