// Logisim project CPU Design.circ as structural Verilog: 7 circuits, main circuit main
module main (
);


  // Notes on the sheet:
  //   Please don't copy. Use as a reference only.
endmodule

module RF (
  input  [15:0] Write_Data,
  input  [3:0] Read_Register_1__RS,
  input  WE,
  input  [3:0] Read_Register_2__RT,
  input  [3:0] Write_Register__RD,
  input  Clock,
  input  CLR,
  output [15:0] Read_Data_1,
  output [15:0] Read_Data_2
);

  wire demultiplexer_1_out0, demultiplexer_1_out1, demultiplexer_1_out2, demultiplexer_1_out3,
       demultiplexer_1_out4, demultiplexer_1_out5, demultiplexer_1_out6, demultiplexer_1_out7,
       demultiplexer_1_out8, demultiplexer_1_out9, demultiplexer_1_out10, demultiplexer_1_out11,
       demultiplexer_1_out12, demultiplexer_1_out13, demultiplexer_1_out14, demultiplexer_1_out15;
  wire [15:0] _0___zero_q, _1___t0_q, _2___t1_q, _3___t2_q, _4___t3_q, _5___t4_q, _6___t5_q, _7___t6_q,
       _8___S1_q, _9___S2_q, _10___S3_q, _11___S4_q, _12___S5_q, _13___S6_q, _14___S7_q, _15___S8_q;

  Demultiplexer #(.select(4)) demultiplexer_1 (
    .out0(demultiplexer_1_out0), .out1(demultiplexer_1_out1), .out2(demultiplexer_1_out2),
    .out3(demultiplexer_1_out3), .out4(demultiplexer_1_out4), .out5(demultiplexer_1_out5),
    .out6(demultiplexer_1_out6), .out7(demultiplexer_1_out7), .out8(demultiplexer_1_out8),
    .out9(demultiplexer_1_out9), .out10(demultiplexer_1_out10), .out11(demultiplexer_1_out11),
    .out12(demultiplexer_1_out12), .out13(demultiplexer_1_out13), .out14(demultiplexer_1_out14),
    .out15(demultiplexer_1_out15), .in(WE), .sel(Write_Register__RD));  // open: en
  Register #(.width(16)) _0___zero (.D(Write_Data), .en(demultiplexer_1_out0), .Q(_0___zero_q), .clk(Clock), .clr(CLR));
  Register #(.width(16)) _1___t0 (.D(Write_Data), .en(demultiplexer_1_out1), .Q(_1___t0_q), .clk(Clock), .clr(CLR));
  Register #(.width(16)) _2___t1 (.D(Write_Data), .en(demultiplexer_1_out2), .Q(_2___t1_q), .clk(Clock), .clr(CLR));
  Register #(.width(16)) _3___t2 (.D(Write_Data), .en(demultiplexer_1_out3), .Q(_3___t2_q), .clk(Clock), .clr(CLR));
  Register #(.width(16)) _4___t3 (.D(Write_Data), .en(demultiplexer_1_out4), .Q(_4___t3_q), .clk(Clock), .clr(CLR));
  Register #(.width(16)) _5___t4 (.D(Write_Data), .en(demultiplexer_1_out5), .Q(_5___t4_q), .clk(Clock), .clr(CLR));
  Register #(.width(16)) _6___t5 (.D(Write_Data), .en(demultiplexer_1_out6), .Q(_6___t5_q), .clk(Clock), .clr(CLR));
  Register #(.width(16)) _7___t6 (.D(Write_Data), .en(demultiplexer_1_out7), .Q(_7___t6_q), .clk(Clock), .clr(CLR));
  Register #(.width(16)) _8___S1 (.D(Write_Data), .en(demultiplexer_1_out8), .Q(_8___S1_q), .clk(Clock), .clr(CLR));
  Register #(.width(16)) _9___S2 (.D(Write_Data), .en(demultiplexer_1_out9), .Q(_9___S2_q), .clk(Clock), .clr(CLR));
  Register #(.width(16)) _10___S3 (.D(Write_Data), .en(demultiplexer_1_out10), .Q(_10___S3_q), .clk(Clock), .clr(CLR));
  Register #(.width(16)) _11___S4 (.D(Write_Data), .en(demultiplexer_1_out11), .Q(_11___S4_q), .clk(Clock), .clr(CLR));
  Register #(.width(16)) _12___S5 (.D(Write_Data), .en(demultiplexer_1_out12), .Q(_12___S5_q), .clk(Clock), .clr(CLR));
  Register #(.width(16)) _13___S6 (.D(Write_Data), .en(demultiplexer_1_out13), .Q(_13___S6_q), .clk(Clock), .clr(CLR));
  Register #(.width(16)) _14___S7 (.D(Write_Data), .en(demultiplexer_1_out14), .Q(_14___S7_q), .clk(Clock), .clr(CLR));
  Register #(.width(16)) _15___S8 (.D(Write_Data), .en(demultiplexer_1_out15), .Q(_15___S8_q), .clk(Clock), .clr(CLR));
  Multiplexer #(.select(4), .width(16)) multiplexer_1 (
    .in0(_0___zero_q), .in1(_1___t0_q), .in2(_2___t1_q), .in3(_3___t2_q), .in4(_4___t3_q), .in5(_5___t4_q),
    .in6(_6___t5_q), .in7(_7___t6_q), .in8(_8___S1_q), .in9(_9___S2_q), .in10(_10___S3_q), .in11(_11___S4_q),
    .in12(_12___S5_q), .in13(_13___S6_q), .in14(_14___S7_q), .in15(_15___S8_q), .out(Read_Data_1),
    .sel(Read_Register_1__RS));  // open: en
  Multiplexer #(.select(4), .width(16)) multiplexer_2 (
    .in0(_0___zero_q), .in1(_1___t0_q), .in2(_2___t1_q), .in3(_3___t2_q), .in4(_4___t3_q), .in5(_5___t4_q),
    .in6(_6___t5_q), .in7(_7___t6_q), .in8(_8___S1_q), .in9(_9___S2_q), .in10(_10___S3_q), .in11(_11___S4_q),
    .in12(_12___S5_q), .in13(_13___S6_q), .in14(_14___S7_q), .in15(_15___S8_q), .out(Read_Data_2),
    .sel(Read_Register_2__RT));  // open: en

  // Notes on the sheet:
  //   Total registers = 16
  //   RS=RT=RD=4bit, Data bit = 16
  //   16bit ALU
endmodule

module _1_bit_ALU (
  input  A,
  input  B,
  input  [1:0] Selector,
  input  Cin,
  output Result,
  output Cout
);

  wire adder_1_out, and_1_out, and_2_out, multiplexer_1_out, not_1_out, or_1_out;

  Multiplexer multiplexer_1 (.in0(B), .in1(not_1_out), .out(multiplexer_1_out), .sel(and_2_out));  // open: en
  not not_1 (not_1_out, B);
  and and_1 (and_1_out, A, B);
  or or_1 (or_1_out, A, B);
  Adder #(.width(1)) adder_1 (.a(A), .b(multiplexer_1_out), .out(adder_1_out), .cin(Cin), .cout(Cout));
  and and_2 (and_2_out, Selector[0], Selector[1]);
  Multiplexer #(.select(2)) multiplexer_2 (
    .in0(and_1_out), .in1(or_1_out), .in2(adder_1_out), .in3(adder_1_out), .out(Result), .sel(Selector));  // open: en
endmodule

module _16_bit_ALU (
  input  [15:0] A,
  input  Cin,
  input  [1:0] Selector,
  input  [15:0] B,
  output [15:0] Result,
  output Cout
);

  wire n1_bit_alu_1_cout, n1_bit_alu_2_cout, n1_bit_alu_3_cout, n1_bit_alu_4_cout, n1_bit_alu_8_cout,
       n1_bit_alu_9_cout, n1_bit_alu_10_cout, n1_bit_alu_11_cout, n1_bit_alu_12_cout, n1_bit_alu_13_cout,
       n1_bit_alu_14_cout, n1_bit_alu_15_cout;

  _1_bit_ALU u_1_bit_alu_1 (
    .Cin(Cin), .Result(Result[0]), .Cout(n1_bit_alu_1_cout), .A(A[0]), .B(B[0]), .Selector(Selector));
  _1_bit_ALU u_1_bit_alu_2 (
    .Cin(n1_bit_alu_1_cout), .Result(Result[1]), .Cout(n1_bit_alu_2_cout), .A(A[1]), .B(B[1]),
    .Selector(Selector));
  _1_bit_ALU u_1_bit_alu_3 (
    .Cin(n1_bit_alu_2_cout), .Result(Result[2]), .Cout(n1_bit_alu_3_cout), .A(A[2]), .B(B[2]),
    .Selector(Selector));
  _1_bit_ALU u_1_bit_alu_4 (
    .Cin(n1_bit_alu_3_cout), .Result(Result[3]), .Cout(n1_bit_alu_4_cout), .A(A[3]), .B(B[3]),
    .Selector(Selector));
  _1_bit_ALU u_1_bit_alu_5 (
    .Cin(n1_bit_alu_4_cout), .Result(Result[4]), .A(A[4]), .B(B[4]), .Selector(Selector));  // open: Cout
  _1_bit_ALU u_1_bit_alu_6 (.Result(Result[5]), .A(A[5]), .B(B[5]), .Selector(Selector));  // open: Cin, Cout
  _1_bit_ALU u_1_bit_alu_7 (.Result(Result[6]), .A(A[6]), .B(B[6]), .Selector(Selector));  // open: Cin, Cout
  _1_bit_ALU u_1_bit_alu_8 (
    .Result(Result[7]), .Cout(n1_bit_alu_8_cout), .A(A[7]), .B(B[7]), .Selector(Selector));  // open: Cin
  _1_bit_ALU u_1_bit_alu_9 (
    .Cin(n1_bit_alu_8_cout), .Result(Result[8]), .Cout(n1_bit_alu_9_cout), .A(A[8]), .B(B[8]),
    .Selector(Selector));
  _1_bit_ALU u_1_bit_alu_10 (
    .Cin(n1_bit_alu_9_cout), .Result(Result[9]), .Cout(n1_bit_alu_10_cout), .A(A[9]), .B(B[9]),
    .Selector(Selector));
  _1_bit_ALU u_1_bit_alu_11 (
    .Cin(n1_bit_alu_10_cout), .Result(Result[10]), .Cout(n1_bit_alu_11_cout), .A(A[10]), .B(B[10]),
    .Selector(Selector));
  _1_bit_ALU u_1_bit_alu_12 (
    .Cin(n1_bit_alu_11_cout), .Result(Result[11]), .Cout(n1_bit_alu_12_cout), .A(A[11]), .B(B[11]),
    .Selector(Selector));
  _1_bit_ALU u_1_bit_alu_13 (
    .Cin(n1_bit_alu_12_cout), .Result(Result[12]), .Cout(n1_bit_alu_13_cout), .A(A[12]), .B(B[12]),
    .Selector(Selector));
  _1_bit_ALU u_1_bit_alu_14 (
    .Cin(n1_bit_alu_13_cout), .Result(Result[13]), .Cout(n1_bit_alu_14_cout), .A(A[13]), .B(B[13]),
    .Selector(Selector));
  _1_bit_ALU u_1_bit_alu_15 (
    .Cin(n1_bit_alu_14_cout), .Result(Result[14]), .Cout(n1_bit_alu_15_cout), .A(A[14]), .B(B[14]),
    .Selector(Selector));
  _1_bit_ALU u_1_bit_alu_16 (
    .Cin(n1_bit_alu_15_cout), .Result(Result[15]), .Cout(Cout), .A(A[15]), .B(B[15]), .Selector(Selector));

  // Other names for the same wires on the sheet: R1 = Result[0]; R2 = Result[1]; R3 = Result[2]; R4 = Result[3];
  //   R5 = Result[4]; R6 = Result[5]; R7 = Result[6]; R8 = Result[7]; R9 = Result[8]; R10 = Result[9];
  //   R11 = Result[10]; R12 = Result[11]; S[1:0] = Selector
endmodule

module IF (
  input  CLK,
  input  CLR,
  output [15:0] Instruction
);

  wire [1:0] adder_1_out, PC_q;

  Register #(.width(2)) PC (.D(adder_1_out), .Q(PC_q), .clk(CLK), .clr(CLR));  // open: en
  Adder #(.width(2)) adder_1 (.a(2'b01), .b(PC_q), .out(adder_1_out));  // open: cin, cout
  ROM #(.addrWidth(2), .dataWidth(16)) rom_1 (.addr(PC_q), .data(Instruction));  // open: sel

  // Notes on the sheet:
  //   contents of rom_1 (hex, n*v repeats v):
  //   2678
endmodule

module R_Type_Data_Path (
  input  CLK,
  input  CLR,
  input  WE
);

  wire [1:0] bit_extender_1_out;
  wire [15:0] if_1_instruction, n16_bit_alu_1_result, rf_1_read_data_1, rf_1_read_data_2;

  IF if_1 (.CLK(CLK), .CLR(CLR), .Instruction(if_1_instruction));
  RF rf_1 (
    .Write_Data(n16_bit_alu_1_result), .Clock(CLK), .Read_Data_1(rf_1_read_data_1),
    .Read_Data_2(rf_1_read_data_2), .Write_Register__RD(if_1_instruction[3:0]),
    .Read_Register_1__RS(if_1_instruction[11:8]), .Read_Register_2__RT(if_1_instruction[7:4]), .WE(WE),
    .CLR(CLR));
  Bit_Extender #(.in_width(4), .out_width(2)) bit_extender_1 (.in(if_1_instruction[15:12]), .out(bit_extender_1_out));
  _16_bit_ALU u_16_bit_alu_1 (
    .A(rf_1_read_data_1), .Result(n16_bit_alu_1_result), .Selector(bit_extender_1_out), .B(rf_1_read_data_2));  // open: Cin, Cout
endmodule

module I_Type_Data_Path (
  input  CLK,
  input  CLR,
  input  WE,
  input  MemWrite,
  input  MemRead
);

  wire [1:0] adder_1_out, bit_extender_2_out, bit_extender_3_out, PC_q;
  wire [15:0] bit_extender_1_out, n16_bit_alu_1_result, ram_1_data, rf_1_read_data_1, rf_1_read_data_2,
       rom_1_data;

  Register #(.width(2)) PC (.D(adder_1_out), .Q(PC_q), .clk(CLK), .clr(CLR));  // open: en
  Adder #(.width(2)) adder_1 (.a(2'b01), .b(PC_q), .out(adder_1_out));  // open: cin, cout
  ROM #(.addrWidth(2), .dataWidth(16)) rom_1 (.addr(PC_q), .data(rom_1_data));  // open: sel
  assign bit_extender_1_out = {{12{1'b0}}, rom_1_data[3:0]};  // Bit_Extender bit_extender_1
  RF rf_1 (
    .Write_Data(ram_1_data), .Clock(CLK), .Read_Data_1(rf_1_read_data_1), .Read_Data_2(rf_1_read_data_2),
    .Write_Register__RD(rom_1_data[7:4]), .Read_Register_1__RS(rom_1_data[11:8]),
    .Read_Register_2__RT(rom_1_data[7:4]), .WE(WE), .CLR(CLR));
  Bit_Extender #(.in_width(4), .out_width(2)) bit_extender_2 (.in(rom_1_data[15:12]), .out(bit_extender_2_out));
  _16_bit_ALU u_16_bit_alu_1 (
    .A(rf_1_read_data_1), .Result(n16_bit_alu_1_result), .Selector(bit_extender_2_out), .B(bit_extender_1_out));  // open: Cin, Cout
  Bit_Extender #(.in_width(16), .out_width(2)) bit_extender_3 (.in(n16_bit_alu_1_result), .out(bit_extender_3_out));
  RAM #(.addrWidth(2), .dataWidth(16), .bus("separate")) ram_1 (
    .addr(bit_extender_3_out), .din(rf_1_read_data_2), .data(ram_1_data), .str(MemWrite), .clk(CLK),
    .ld(MemRead));  // open: sel, clr

  // Notes on the sheet:
  //   contents of rom_1 (hex, n*v repeats v):
  //   2061 2060
endmodule
