// Logisim project Lab 03.circ as structural Verilog: 1 circuit, main circuit main
module main (
  input  A2,
  input  A1,
  input  B2,
  input  B1,
  input  in_5,
  output S1,
  output S4,
  output S3,
  output S2
);

  wire [0:0] and_2_out;
  wire [1:0] and_3_out;
  wire [3:3] adder_1_out;

  and and_1 (S1, A1, B1);
  and and_2 (and_2_out[0], A1, B2);
  and and_3 (and_3_out[0], A2, B1);
  and and_4 (and_3_out[1], A2, B2);
  Adder #(.width(4)) adder_1 (
    .a({{3{in_5}}, and_2_out[0]}), .b({{2{in_5}}, and_3_out}), .out({adder_1_out[3], S4, S3, S2}), .cin(in_5));  // open: cout

  // Notes on the sheet:
  //   4 bit Adder
  //   Lab: 03
  //   Group: 03
endmodule
