// Logisim project Lab 04.circ as structural Verilog: 1 circuit, main circuit main
module main (
  input  M,
  output out_2,
  output out_3
);

  wire clock_1_out, xor_1_out, xor_2_out, xor_3_out;

  xor xor_1 (xor_1_out, M, out_3);
  xor xor_2 (xor_2_out, out_2, xor_1_out);
  xor xor_3 (xor_3_out, 1'b1, out_3);
  Clock clock_1 (.out(clock_1_out));
  D_Flip_Flop d_ff_1 (.clk(clock_1_out), .D(xor_2_out), .Q(out_2));  // open: Qn, preset, en, reset
  D_Flip_Flop d_ff_2 (.clk(clock_1_out), .D(xor_3_out), .Q(out_3));  // open: Qn, preset, en, reset

  // Notes on the sheet:
  //   Lab: 04
  //   Group: 03
endmodule
