// Logisim project Lab 05.circ as structural Verilog
module RF__sec_10 (
  input  [3:0] Write_Data,
  input  [1:0] Read_Register_1__RS,
  input  [1:0] Write_Register__RD,
  input  [1:0] Read_Register_2__RT,
  input  Clock,
  output [3:0] Read_Data_1,
  output [3:0] Read_Data_2
);

  wire decoder_1_out0, decoder_1_out1, decoder_1_out2, decoder_1_out3;
  wire [3:0] _0___zero_q, _1___t0_q, _2___S0_q, _3___S1_q;

  Decoder #(.select(2)) decoder_1 (
    .out0(decoder_1_out0), .out1(decoder_1_out1), .out2(decoder_1_out2), .out3(decoder_1_out3),
    .sel(Write_Register__RD));  // open: en
  Register #(.width(4)) _0___zero (.D(Write_Data), .en(decoder_1_out0), .Q(_0___zero_q), .clk(Clock));  // open: clr
  Register #(.width(4)) _1___t0 (.D(Write_Data), .en(decoder_1_out1), .Q(_1___t0_q), .clk(Clock));  // open: clr
  Register #(.width(4)) _2___S0 (.D(Write_Data), .en(decoder_1_out2), .Q(_2___S0_q), .clk(Clock));  // open: clr
  Register #(.width(4)) _3___S1 (.D(Write_Data), .en(decoder_1_out3), .Q(_3___S1_q), .clk(Clock));  // open: clr
  Multiplexer #(.select(2), .width(4)) multiplexer_1 (
    .in0(_0___zero_q), .in1(_1___t0_q), .in2(_2___S0_q), .in3(_3___S1_q), .out(Read_Data_1),
    .sel(Read_Register_1__RS));  // open: en
  Multiplexer #(.select(2), .width(4)) multiplexer_2 (
    .in0(_0___zero_q), .in1(_1___t0_q), .in2(_2___S0_q), .in3(_3___S1_q), .out(Read_Data_2),
    .sel(Read_Register_2__RT));  // open: en

  // Notes on the sheet:
  //   Group: 03
  //   RS=RT=RD=2bit, Data bit = 4
endmodule
