// Logisim project Pipeline.circ as structural Verilog: 3 circuits, main circuit main
module main (
  input  [31:0] A,
  input  [31:0] B,
  input  Clock,
  input  Clear,
  output [31:0] Y,
  output [31:0] Z
);

  wire [31:0] if_id_1_output1, if_id_1_output2;

  IF_ID if_id_1 (
    .Input1(A), .Input2(B), .Clock(Clock), .Clear(Clear), .Output1(if_id_1_output1), .Output2(if_id_1_output2));
  // Probe on if_id_1_output1
  ID_EX id_ex_1 (
    .Input1(if_id_1_output1), .Input3(if_id_1_output2), .Clock(Clock), .Clear(Clear), .Output1(Y), .Output3(Z));  // open: Input2, Input4, Input5, Output2, Output4, Output5
  // Probe on if_id_1_output2
endmodule

module IF_ID (
  input  [31:0] Input1,
  input  [31:0] Input2,
  input  Clock,
  input  Clear,
  output [31:0] Output1,
  output [31:0] Output2
);

  Register #(.width(32)) register_1 (.D(Input1), .Q(Output1), .clk(Clock), .clr(Clear));  // open: en
  Register #(.width(32)) register_2 (.D(Input2), .Q(Output2), .clk(Clock), .clr(Clear));  // open: en
endmodule

module ID_EX (
  input  [31:0] Input1,
  input  [31:0] Input2,
  input  [31:0] Input3,
  input  [31:0] Input4,
  input  [4:0] Input5,
  input  Clock,
  input  Clear,
  output [31:0] Output1,
  output [31:0] Output2,
  output [31:0] Output3,
  output [31:0] Output4,
  output [4:0] Output5
);

  Register #(.width(32)) register_1 (.D(Input1), .Q(Output1), .clk(Clock), .clr(Clear));  // open: en
  Register #(.width(32)) register_2 (.D(Input2), .Q(Output2), .clk(Clock), .clr(Clear));  // open: en
  Register #(.width(32)) register_3 (.D(Input3), .Q(Output3), .clk(Clock), .clr(Clear));  // open: en
  Register #(.width(32)) register_4 (.D(Input4), .Q(Output4), .clk(Clock), .clr(Clear));  // open: en
  Register #(.width(5)) register_5 (.D(Input5), .Q(Output5), .clk(Clock), .clr(Clear));  // open: en
endmodule
