// Logisim project RF.circ as structural Verilog
module RF (
  input  [15:0] Write_Data,
  input  [3:0] Read_Register_1__RS,
  input  [3:0] Write_Register__RD,
  input  [3:0] Read_Register_2__RT,
  input  Clock,
  output [15:0] Read_Data_1,
  output [15:0] Read_Data_2
);

  wire _5, _6, decoder_1_out0, decoder_1_out1, decoder_1_out2, decoder_1_out3, decoder_1_out4;
  wire [15:0] _0___zero_q, _1___t0_q, _2___t1_q, _3___t2_q, register_1_q, register_2_q;

  Decoder #(.select(4)) decoder_1 (
    .out0(decoder_1_out0), .out1(decoder_1_out1), .out2(decoder_1_out2), .out3(decoder_1_out3),
    .out4(decoder_1_out4), .out5(_5), .out6(_6), .sel(Write_Register__RD));  // open: out7, out8, out9, out10, out11, out12, out13, out14, out15, en
  Register #(.width(16)) _0___zero (.D(Write_Data), .en(decoder_1_out0), .Q(_0___zero_q), .clk(Clock));  // open: clr
  Register #(.width(16)) _1___t0 (.D(Write_Data), .en(decoder_1_out1), .Q(_1___t0_q), .clk(Clock));  // open: clr
  Register #(.width(16)) _2___t1 (.D(Write_Data), .en(decoder_1_out2), .Q(_2___t1_q), .clk(Clock));  // open: clr
  Register #(.width(16)) _3___t2 (.D(Write_Data), .en(decoder_1_out3), .Q(_3___t2_q), .clk(Clock));  // open: clr
  Register #(.width(16)) register_1 (.D(Write_Data), .en(decoder_1_out4), .Q(register_1_q), .clk(Clock));  // open: clr
  Register #(.width(16)) register_2 (.D(Write_Data), .en(_5), .Q(register_2_q), .clk(Clock));  // open: clr
  Register #(.width(16)) register_3 (.D(Write_Data), .en(_6), .clk(Clock));  // open: Q, clr
  Register #(.width(16)) register_4 (.D(Write_Data), .clk(Clock));  // open: en, Q, clr
  Register #(.width(16)) register_5 (.D(Write_Data), .clk(Clock));  // open: en, Q, clr
  Register #(.width(16)) register_6 (.D(Write_Data), .clk(Clock));  // open: en, Q, clr
  Register #(.width(16)) register_7 (.D(Write_Data), .clk(Clock));  // open: en, Q, clr
  Register #(.width(16)) register_8 (.D(Write_Data), .clk(Clock));  // open: en, Q, clr
  Register #(.width(16)) register_9 (.D(Write_Data), .clk(Clock));  // open: en, Q, clr
  Register #(.width(16)) register_10 (.D(Write_Data), .clk(Clock));  // open: en, Q, clr
  Register #(.width(16)) register_11 (.D(Write_Data), .clk(Clock));  // open: en, Q, clr
  Register #(.width(16)) _15 (.D(Write_Data), .clk(Clock));  // open: en, Q, clr
  Multiplexer #(.select(4), .width(16)) multiplexer_1 (
    .in0(_0___zero_q), .in1(_1___t0_q), .in2(_2___t1_q), .in3(_3___t2_q), .in4(register_1_q),
    .in5(register_2_q), .out(Read_Data_1), .sel(Read_Register_1__RS));  // open: in6, in7, in8, in9, in10, in11, in12, in13, in14, in15, en
  Multiplexer #(.select(4), .width(16)) multiplexer_2 (
    .in0(_0___zero_q), .in1(_1___t0_q), .in2(_2___t1_q), .in3(_3___t2_q), .in4(register_1_q),
    .in5(register_2_q), .out(Read_Data_2), .sel(Read_Register_2__RT));  // open: in6, in7, in8, in9, in10, in11, in12, in13, in14, in15, en

  // Notes on the sheet:
  //   RS=RT=RD=4bit, Data bit = 16
  //   Total registers = 16
  //   16bit ALU
endmodule

module RF__sec_10 (
  input  [3:0] Write_Data,
  input  [1:0] Read_Register_1__RS,
  input  [1:0] Write_Register__RD,
  input  [1:0] Read_Register_2__RT,
  input  Clock,
  output [3:0] Read_Data_1,
  output [3:0] Read_Data_2
);

  wire decoder_1_out0, decoder_1_out1, decoder_1_out2, decoder_1_out3;
  wire [3:0] _0___zero_q, _1___t0_q, _2___s0_q, _3___s1_q;

  Decoder #(.select(2)) decoder_1 (
    .out0(decoder_1_out0), .out1(decoder_1_out1), .out2(decoder_1_out2), .out3(decoder_1_out3),
    .sel(Write_Register__RD));  // open: en
  Register #(.width(4)) _0___zero (.D(Write_Data), .en(decoder_1_out0), .Q(_0___zero_q), .clk(Clock));  // open: clr
  Register #(.width(4)) _1___t0 (.D(Write_Data), .en(decoder_1_out1), .Q(_1___t0_q), .clk(Clock));  // open: clr
  Register #(.width(4)) _2___s0 (.D(Write_Data), .en(decoder_1_out2), .Q(_2___s0_q), .clk(Clock));  // open: clr
  Register #(.width(4)) _3___s1 (.D(Write_Data), .en(decoder_1_out3), .Q(_3___s1_q), .clk(Clock));  // open: clr
  Multiplexer #(.select(2), .width(4)) multiplexer_1 (
    .in0(_0___zero_q), .in1(_1___t0_q), .in2(_2___s0_q), .in3(_3___s1_q), .out(Read_Data_1),
    .sel(Read_Register_1__RS));  // open: en
  Multiplexer #(.select(2), .width(4)) multiplexer_2 (
    .in0(_0___zero_q), .in1(_1___t0_q), .in2(_2___s0_q), .in3(_3___s1_q), .out(Read_Data_2),
    .sel(Read_Register_2__RT));  // open: en

  // Notes on the sheet:
  //   RS=RT=RD=2bit, Data bit = 4
endmodule
